// Logisim project CA_Project_1_3.circ as structural Verilog: 1 circuit, main circuit main
module main (
  input  in_1,
  input  in_2,
  input  in_3,
  input  in_4,
  input  in_5,
  input  in_6,
  input  in_7,
  output out_8,
  output out_9,
  output out_10,
  output out_11
);

  wire and_1_out, nand_2_out, NOT_2_out, NOT_out;

  and and_1 (and_1_out, in_1, in_2);
  nand nand_1 (out_9, in_3, in_3);
  nand NOT (NOT_out, in_4, in_4);
  nand NOT_2 (NOT_2_out, in_5, in_5);
  nand nand_2 (nand_2_out, in_6, in_7);
  not not_3 (out_8, and_1_out);
  nand nand_3 (out_10, NOT_out, NOT_2_out);
  nand nand_4 (out_11, nand_2_out, nand_2_out);

  // Notes on the sheet:
  //   NAND
  //   NOT
  //   OR
  //   AND
endmodule
