// Logisim project CA_Project_1_5.circ as structural Verilog: 1 circuit, main circuit main
module main (
  input  A,
  input  B,
  input  C
);

  wire A_B_C_out, A_B_nC_out, A_nB_C_out, A_nB_nC_out, and_1_out, nA_B_C_out, nA_B_nC_out, nA_nB_nC_out,
       not_1_out, not_2_out, not_3_out, or_1_out, or_2_out, or_3_out, or_4_out, or_5_out, or_6_out, or_7_out,
       or_8_out, or_9_out, or_10_out, or_11_out;

  and nA_nB_nC (nA_nB_nC_out, not_1_out, not_2_out, not_3_out);
  or or_1 (or_1_out, nA_nB_nC_out, and_1_out);
  or or_2 (or_2_out, nA_nB_nC_out, or_3_out, A_nB_C_out, or_3_out, or_9_out);
  and and_1 (and_1_out, not_1_out, not_2_out, C);
  not not_1 (not_1_out, A);
  and nA_B_nC (nA_B_nC_out, not_1_out, B, not_3_out);
  or or_3 (or_3_out, nA_B_nC_out, nA_B_C_out);
  or or_4 (or_4_out, or_1_out, or_3_out, A_nB_nC_out, A_B_C_out);
  not not_2 (not_2_out, B);
  and nA_B_C (nA_B_C_out, not_1_out, B, C);
  or or_5 (or_5_out, or_1_out, nA_B_C_out, or_6_out, or_9_out);
  and A_nB_nC (A_nB_nC_out, A, not_2_out, not_3_out);
  _7_Segment_Display u_7_segment_display_1 (
    .g(or_11_out), .f(or_10_out), .a(or_2_out), .b(or_4_out), .e(or_8_out), .d(or_7_out), .c(or_5_out));  // open: dp
  not not_3 (not_3_out, C);
  and A_nB_C (A_nB_C_out, A, not_2_out, C);
  or or_6 (or_6_out, A_nB_nC_out, A_nB_C_out);
  or or_7 (or_7_out, nA_nB_nC_out, or_3_out, A_nB_C_out, A_B_nC_out);
  and A_B_nC (A_B_nC_out, A, B, not_3_out);
  or or_8 (or_8_out, nA_nB_nC_out, nA_B_nC_out, A_B_nC_out);
  and A_B_C (A_B_C_out, A, B, C);
  or or_9 (or_9_out, A_B_nC_out, A_B_C_out);
  or or_10 (or_10_out, nA_nB_nC_out, or_6_out, A_B_nC_out);
  or or_11 (or_11_out, or_3_out, or_6_out, A_B_nC_out);

  // Notes on the sheet:
  //   !A.!B.C
endmodule
