// Logisim project CA_Project_2_1-2.circ as structural Verilog: 2 circuits, main circuit 1-Bit Full Adder
// 1-Bit\nAdder
module _1_Bit_Full_Adder (
  input  A,
  input  B,
  input  Cin,
  output S,
  output Cout
);

  wire A_prime_B_prime_Ci_out, A_prime_BCi_prime_out, AB_out, AB_prime_Ci_prime_out, ABCi_out, ACi_out,
       BCi_out;

  and A_prime_B_prime_Ci (A_prime_B_prime_Ci_out, ~A, ~B, Cin);  // AND_Gate
  and A_prime_BCi_prime (A_prime_BCi_prime_out, ~A, B, ~Cin);  // AND_Gate
  or u_S (S, A_prime_B_prime_Ci_out, A_prime_BCi_prime_out, AB_prime_Ci_prime_out, ABCi_out);
  and AB_prime_Ci_prime (AB_prime_Ci_prime_out, A, ~B, ~Cin);  // AND_Gate
  and ABCi (ABCi_out, A, B, Cin);
  and ACi (ACi_out, A, Cin);
  and BCi (BCi_out, B, Cin);
  or u_Cout (Cout, ACi_out, BCi_out, AB_out);
  and AB (AB_out, A, B);
endmodule

module _12_bit_Two_s_Complement_Ripple_Carry_Adder (
  input  Cin,
  input  [11:0] in_2,
  input  [11:0] in_3,
  output [11:0] Som,
  output Overflow
);

  wire n1_bit_full_adder_1_cout, n1_bit_full_adder_2_cout, n1_bit_full_adder_3_cout,
       n1_bit_full_adder_4_cout, n1_bit_full_adder_5_cout, n1_bit_full_adder_6_cout,
       n1_bit_full_adder_7_cout, n1_bit_full_adder_8_cout, n1_bit_full_adder_9_cout,
       n1_bit_full_adder_10_cout, n1_bit_full_adder_11_cout, n1_bit_full_adder_12_cout;

  _1_Bit_Full_Adder u_1_bit_full_adder_1 (
    .A(in_2[0]), .B(in_3[0]), .Cin(Cin), .S(Som[0]), .Cout(n1_bit_full_adder_1_cout));
  _1_Bit_Full_Adder u_1_bit_full_adder_2 (
    .A(in_2[1]), .B(in_3[1]), .Cin(n1_bit_full_adder_1_cout), .S(Som[1]), .Cout(n1_bit_full_adder_2_cout));
  _1_Bit_Full_Adder u_1_bit_full_adder_3 (
    .A(in_2[2]), .B(in_3[2]), .Cin(n1_bit_full_adder_2_cout), .S(Som[2]), .Cout(n1_bit_full_adder_3_cout));
  _1_Bit_Full_Adder u_1_bit_full_adder_4 (
    .A(in_2[3]), .B(in_3[3]), .Cin(n1_bit_full_adder_3_cout), .S(Som[3]), .Cout(n1_bit_full_adder_4_cout));
  _1_Bit_Full_Adder u_1_bit_full_adder_5 (
    .A(in_2[4]), .B(in_3[4]), .Cin(n1_bit_full_adder_4_cout), .S(Som[4]), .Cout(n1_bit_full_adder_5_cout));
  _1_Bit_Full_Adder u_1_bit_full_adder_6 (
    .A(in_2[5]), .B(in_3[5]), .Cin(n1_bit_full_adder_5_cout), .S(Som[5]), .Cout(n1_bit_full_adder_6_cout));
  _1_Bit_Full_Adder u_1_bit_full_adder_7 (
    .A(in_2[6]), .B(in_3[6]), .Cin(n1_bit_full_adder_6_cout), .S(Som[6]), .Cout(n1_bit_full_adder_7_cout));
  _1_Bit_Full_Adder u_1_bit_full_adder_8 (
    .A(in_2[7]), .B(in_3[7]), .Cin(n1_bit_full_adder_7_cout), .S(Som[7]), .Cout(n1_bit_full_adder_8_cout));
  _1_Bit_Full_Adder u_1_bit_full_adder_9 (
    .A(in_2[8]), .B(in_3[8]), .Cin(n1_bit_full_adder_8_cout), .S(Som[8]), .Cout(n1_bit_full_adder_9_cout));
  _1_Bit_Full_Adder u_1_bit_full_adder_10 (
    .A(in_2[9]), .B(in_3[9]), .Cin(n1_bit_full_adder_9_cout), .S(Som[9]), .Cout(n1_bit_full_adder_10_cout));
  _1_Bit_Full_Adder u_1_bit_full_adder_11 (
    .A(in_2[10]), .B(in_3[10]), .Cin(n1_bit_full_adder_10_cout), .S(Som[10]), .Cout(n1_bit_full_adder_11_cout));
  _1_Bit_Full_Adder u_1_bit_full_adder_12 (
    .A(in_2[11]), .B(in_3[11]), .Cin(n1_bit_full_adder_11_cout), .S(Som[11]), .Cout(n1_bit_full_adder_12_cout));
  xor xor_1 (Overflow, n1_bit_full_adder_11_cout, n1_bit_full_adder_12_cout);
endmodule
