// Logisim project CA_Project_2_3-4.circ as structural Verilog: 5 circuits, main circuit 1-Bit Adder
// 1-Bit\nAdder
module _1_Bit_Adder (
  input  A,
  input  B,
  input  Cin,
  output S
);

  wire xor_1_out;

  xor xor_1 (xor_1_out, A, B);
  xor xor_2 (S, xor_1_out, Cin);
endmodule

module Compare (
  input  C_in,
  input  [11:0] A,
  input  [11:0] B,
  output [11:0] S,
  output overflow,
  output [11:0] S_2,
  output overflow_2
);

  // Probe on A
  // Probe on B
  _12_bit_Two_s_Complement_Ripple_Carry_Adder u_12_bit_two_s_complement_ripple_carry_adder_1 (
    .in_2(A), .in_3(B), .Som(S), .Cin(C_in), .Overflow(overflow));
  _12_Bit_CLA u_12_bit_cla_1 (.A(A), .Sum(S_2), .B(B), .C0(C_in), .Overflow(overflow_2));  // open: C4
  // Probe on S
  // Probe on S_2
endmodule

// CLA
module _12_Bit_CLA (
  input  C0,
  input  [11:0] A,
  input  [11:0] B,
  output C4,
  output Overflow,
  output [11:0] Sum
);

  wire cla_unit_1_c1, cla_unit_1_c2, n4_bit_cla_1_c3, n4_bit_cla_1_g0, n4_bit_cla_1_p0, n4_bit_cla_2_g0,
       n4_bit_cla_2_p0, n4_bit_cla_3_g0, n4_bit_cla_3_p0;

  xor xor_1 (Overflow, C4, n4_bit_cla_1_c3);
  _4_Bit_CLA u_4_bit_cla_1 (
    .A(A[11:8]), .B(B[11:8]), .Carry_In(cla_unit_1_c2), .S(Sum[11:8]), .c3(n4_bit_cla_1_c3),
    .P0(n4_bit_cla_1_p0), .G0(n4_bit_cla_1_g0));
  _4_Bit_CLA u_4_bit_cla_2 (
    .A(A[7:4]), .B(B[7:4]), .Carry_In(cla_unit_1_c1), .S(Sum[7:4]), .P0(n4_bit_cla_2_p0), .G0(n4_bit_cla_2_g0));  // open: c3
  CLA_Unit cla_unit_1 (
    .G0(n4_bit_cla_3_g0), .P0(n4_bit_cla_3_p0), .G1(n4_bit_cla_2_g0), .P1(n4_bit_cla_2_p0),
    .G2(n4_bit_cla_1_g0), .P2(n4_bit_cla_1_p0), .C1(cla_unit_1_c1), .C2(cla_unit_1_c2), .C3(C4), .C0(C0));
  _4_Bit_CLA u_4_bit_cla_3 (
    .A(A[3:0]), .B(B[3:0]), .Carry_In(C0), .S(Sum[3:0]), .P0(n4_bit_cla_3_p0), .G0(n4_bit_cla_3_g0));  // open: c3
endmodule

// Carry-Lookahead Unit
module CLA_Unit (
  input  C0,
  input  G0,
  input  P0,
  input  G1,
  input  P1,
  input  G2,
  input  P2,
  output C1,
  output C2,
  output C3
);

  wire P0___c0_out, P0___P1___c0_out, P0___P1___P2___c0_out, P1___G0_out, P1___P2___G0_out, P2___G1_out;

  and P0___c0 (P0___c0_out, C0, P0);
  and P0___P1___c0 (P0___P1___c0_out, C0, P0, P1);
  and P1___G0 (P1___G0_out, P1, G0);
  and P0___P1___P2___c0 (P0___P1___P2___c0_out, P0, P1, P2, C0);
  and P1___P2___G0 (P1___P2___G0_out, P1, P2, G0);
  and P2___G1 (P2___G1_out, P2, G1);
  or u_C1 (C1, G0, P0___c0_out);
  or or_1 (C2, G1, P0___P1___c0_out, P1___G0_out);
  or or_2 (C3, G2, P0___P1___P2___c0_out, P1___P2___G0_out, P2___G1_out);
endmodule

// 4-bit\nCLA
module _4_Bit_CLA (
  input  [3:0] A,
  input  [3:0] B,
  input  Carry_In,
  output [3:0] S,
  output c3,
  output P0,
  output G0
);

  wire c1, c2, g0_out, g1_out, g2_out, g3_out, p0___Ci_out, p0_out, p1___g0_out, p1_out, p1_p0_Ci_out,
       p2___g1_out, p2___p1___g0_out, p2___p1___p0___c0_out, p2_out, p3___g2_out, p3_out, p3_p2_g1_out,
       p3_p2_p1_g0_out;

  or u_p0 (p0_out, A[0], B[0]);
  or p1 (p1_out, A[1], B[1]);
  and u_g0 (g0_out, A[0], B[0]);
  or p2 (p2_out, A[2], B[2]);
  and g1 (g1_out, A[1], B[1]);
  or p3 (p3_out, A[3], B[3]);
  and g2 (g2_out, A[2], B[2]);
  and g3 (g3_out, A[3], B[3]);
  and P0_2 (P0, p0_out, p1_out, p2_out, p3_out);
  and p3___g2 (p3___g2_out, p3_out, g2_out);
  and p3_p2_g1 (p3_p2_g1_out, p2_out, p3_out, g1_out);
  and p3_p2_p1_g0 (p3_p2_p1_g0_out, g0_out, p1_out, p2_out, p3_out);
  and p0___Ci (p0___Ci_out, Carry_In, p0_out);
  and p1___g0 (p1___g0_out, g0_out, p1_out);
  and p1_p0_Ci (p1_p0_Ci_out, Carry_In, p0_out, p1_out);
  and p2___g1 (p2___g1_out, p2_out, g1_out);
  and p2___p1___g0 (p2___p1___g0_out, g0_out, p1_out, p2_out);
  and p2___p1___p0___c0 (p2___p1___p0___c0_out, Carry_In, p0_out, p1_out, p2_out);
  _1_Bit_Adder u_1_bit_adder_1 (.A(A[0]), .B(B[0]), .Cin(Carry_In), .S(S[0]));
  _1_Bit_Adder u_1_bit_adder_2 (.A(A[1]), .B(B[1]), .Cin(c1), .S(S[1]));
  _1_Bit_Adder u_1_bit_adder_3 (.A(A[2]), .B(B[2]), .Cin(c2), .S(S[2]));
  _1_Bit_Adder u_1_bit_adder_4 (.A(A[3]), .B(B[3]), .Cin(c3), .S(S[3]));
  or u_c1 (c1, g0_out, p0___Ci_out);
  or G0_2 (G0, g3_out, p3___g2_out, p3_p2_g1_out, p3_p2_p1_g0_out);
  or u_c3 (c3, g2_out, p2___g1_out, p2___p1___g0_out, p2___p1___p0___c0_out);
  or u_c2 (c2, g1_out, p1___g0_out, p1_p0_Ci_out);

  // Other names for the same wires on the sheet: c0 = Carry_In
endmodule
