// Logisim project CA_Project_4.circ as structural Verilog: 5 circuits, main circuit 12-bit register
module _12_bit_register (
  input  [11:0] D,
  input  reset,
  input  write,
  input  C,
  output [11:0] out_5
);

  wire C_t;

  not not_1 (C_t, C);
  D_Flip_Flop d_ff_1 (.clk(C_t), .D(D[0]), .Q(out_5[0]), .en(write), .reset(reset));  // open: Qn, preset
  D_Flip_Flop d_ff_2 (.clk(C_t), .D(D[1]), .Q(out_5[1]), .en(write), .reset(reset));  // open: Qn, preset
  D_Flip_Flop d_ff_3 (.clk(C_t), .D(D[2]), .Q(out_5[2]), .en(write), .reset(reset));  // open: Qn, preset
  D_Flip_Flop d_ff_4 (.clk(C_t), .D(D[3]), .Q(out_5[3]), .en(write), .reset(reset));  // open: Qn, preset
  D_Flip_Flop d_ff_5 (.clk(C_t), .D(D[4]), .Q(out_5[4]), .en(write), .reset(reset));  // open: Qn, preset
  D_Flip_Flop d_ff_6 (.clk(C_t), .D(D[5]), .Q(out_5[5]), .en(write), .reset(reset));  // open: Qn, preset
  D_Flip_Flop d_ff_7 (.clk(C_t), .D(D[6]), .Q(out_5[6]), .en(write), .reset(reset));  // open: Qn, preset
  D_Flip_Flop d_ff_8 (.clk(C_t), .D(D[7]), .Q(out_5[7]), .en(write), .reset(reset));  // open: Qn, preset
  D_Flip_Flop d_ff_9 (.clk(C_t), .D(D[8]), .Q(out_5[8]), .en(write), .reset(reset));  // open: Qn, preset
  D_Flip_Flop d_ff_10 (.clk(C_t), .D(D[9]), .Q(out_5[9]), .en(write), .reset(reset));  // open: Qn, preset
  D_Flip_Flop d_ff_11 (.clk(C_t), .D(D[10]), .Q(out_5[10]), .en(write), .reset(reset));  // open: Qn, preset
  D_Flip_Flop d_ff_12 (.clk(C_t), .D(D[11]), .Q(out_5[11]), .en(write), .reset(reset));  // open: Qn, preset
endmodule

module register_file (
  input  [2:0] rs,
  input  [2:0] rt,
  input  [2:0] rd,
  input  [11:0] Data,
  input  write,
  input  reset,
  input  C,
  output [11:0] S,
  output [11:0] T
);

  wire and_1_out, and_2_out, and_3_out, and_4_out, and_5_out, and_6_out, and_7_out, decoder_1_out1,
       decoder_1_out2, decoder_1_out3, decoder_1_out4, decoder_1_out5, decoder_1_out6, decoder_1_out7;
  wire [11:0] n12_bit_register_1_out_5, n12_bit_register_2_out_5, n12_bit_register_3_out_5,
       n12_bit_register_4_out_5, n12_bit_register_5_out_5, n12_bit_register_6_out_5,
       n12_bit_register_7_out_5, n12_bit_register_8_out_5;

  Decoder #(.select(3)) decoder_1 (
    .out1(decoder_1_out1), .out2(decoder_1_out2), .out3(decoder_1_out3), .out4(decoder_1_out4),
    .out5(decoder_1_out5), .out6(decoder_1_out6), .out7(decoder_1_out7), .sel(rd), .en(1'b1));  // open: out0
  and and_1 (and_1_out, decoder_1_out1, write);
  and and_2 (and_2_out, decoder_1_out2, write);
  and and_3 (and_3_out, decoder_1_out3, write);
  and and_4 (and_4_out, decoder_1_out4, write);
  and and_5 (and_5_out, decoder_1_out5, write);
  and and_6 (and_6_out, decoder_1_out6, write);
  and and_7 (and_7_out, decoder_1_out7, write);
  _12_bit_register u_12_bit_register_1 (.D(Data), .reset(reset), .write(1'b0), .out_5(n12_bit_register_1_out_5), .C(C));
  _12_bit_register u_12_bit_register_2 (
    .D(Data), .reset(reset), .write(and_1_out), .out_5(n12_bit_register_2_out_5), .C(C));
  _12_bit_register u_12_bit_register_3 (
    .D(Data), .reset(reset), .write(and_2_out), .out_5(n12_bit_register_3_out_5), .C(C));
  _12_bit_register u_12_bit_register_4 (
    .D(Data), .reset(reset), .write(and_3_out), .out_5(n12_bit_register_4_out_5), .C(C));
  _12_bit_register u_12_bit_register_5 (
    .D(Data), .reset(reset), .write(and_4_out), .out_5(n12_bit_register_5_out_5), .C(C));
  _12_bit_register u_12_bit_register_6 (
    .D(Data), .reset(reset), .write(and_5_out), .out_5(n12_bit_register_6_out_5), .C(C));
  _12_bit_register u_12_bit_register_7 (
    .D(Data), .reset(reset), .write(and_6_out), .out_5(n12_bit_register_7_out_5), .C(C));
  _12_bit_register u_12_bit_register_8 (
    .D(Data), .reset(reset), .write(and_7_out), .out_5(n12_bit_register_8_out_5), .C(C));
  Multiplexer #(.select(3), .width(12)) multiplexer_1 (
    .in0(n12_bit_register_1_out_5), .in1(n12_bit_register_2_out_5), .in2(n12_bit_register_3_out_5),
    .in3(n12_bit_register_4_out_5), .in4(n12_bit_register_5_out_5), .in5(n12_bit_register_6_out_5),
    .in6(n12_bit_register_7_out_5), .in7(n12_bit_register_8_out_5), .out(S), .sel(rs), .en(1'b1));
  Multiplexer #(.select(3), .width(12)) multiplexer_2 (
    .in0(n12_bit_register_1_out_5), .in1(n12_bit_register_2_out_5), .in2(n12_bit_register_3_out_5),
    .in3(n12_bit_register_4_out_5), .in4(n12_bit_register_5_out_5), .in5(n12_bit_register_6_out_5),
    .in6(n12_bit_register_7_out_5), .in7(n12_bit_register_8_out_5), .out(T), .sel(rt), .en(1'b1));
endmodule

module counter (
  input  [11:0] D,
  input  C,
  output [11:0] pc
);

  wire comparator_1_eq, comparator_1_gt, or_1_out;
  wire [11:0] n12_bit_cla_1_sum;

  or or_1 (or_1_out, comparator_1_gt, comparator_1_eq);
  Comparator #(.width(12), .mode("unsigned")) comparator_1 (
    .a(pc), .b(D), .gt(comparator_1_gt), .eq(comparator_1_eq));  // open: lt
  _12_bit_register u_12_bit_register_1 (.D(n12_bit_cla_1_sum), .reset(or_1_out), .write(1'b1), .out_5(pc), .C(C));
  _12_Bit_CLA u_12_bit_cla_1 (.A(pc), .Sum(n12_bit_cla_1_sum), .B(12'h1), .C0(1'b0));  // open: C4, Overflow
endmodule

module traffic_light (
);

  wire Clock_out, decoder_1_out0, decoder_1_out1, decoder_1_out2, decoder_1_out3, decoder_1_out4,
       decoder_1_out5, decoder_1_out6, decoder_1_out7, decoder_1_out8, decoder_1_out9, decoder_1_out10,
       decoder_1_out11, decoder_1_out12, decoder_1_out13, decoder_1_out14, decoder_1_out15, decoder_1_out16,
       decoder_1_out17, decoder_1_out18, decoder_1_out19, decoder_1_out20, decoder_1_out21, decoder_1_out22,
       decoder_1_out23, decoder_1_out24, decoder_1_out25, decoder_1_out26, decoder_1_out27, decoder_2_out0,
       decoder_2_out1, decoder_2_out2, decoder_2_out3, decoder_2_out4, decoder_2_out5, decoder_2_out6,
       decoder_2_out7, decoder_2_out8, decoder_2_out9, decoder_2_out10, decoder_2_out11, decoder_2_out12,
       decoder_2_out13, decoder_2_out14, decoder_2_out15, decoder_2_out16, decoder_2_out17, decoder_2_out18,
       decoder_2_out19, decoder_2_out20, decoder_2_out21, decoder_2_out22, decoder_2_out23, decoder_2_out24,
       decoder_2_out25, decoder_2_out26, decoder_2_out27, L1G, L1R, L1Y, L2G, L2R, L2Y, or_4_out, or_7_out;
  wire [11:0] counter_1_pc;

  Clock Clock (.out(Clock_out));
  LED led_1 (.in(L1G));
  LED led_2 (.in(L1Y));
  LED led_3 (.in(L1R));
  LED led_4 (.in(L2G));
  LED led_5 (.in(L2Y));
  LED led_6 (.in(L2R));
  counter counter_1 (.D(12'h1c), .C(Clock_out), .pc(counter_1_pc));
  Decoder #(.select(5)) decoder_1 (
    .out0(decoder_1_out0), .out1(decoder_1_out1), .out2(decoder_1_out2), .out3(decoder_1_out3),
    .out4(decoder_1_out4), .out5(decoder_1_out5), .out6(decoder_1_out6), .out7(decoder_1_out7),
    .out8(decoder_1_out8), .out9(decoder_1_out9), .out10(decoder_1_out10), .out11(decoder_1_out11),
    .out12(decoder_1_out12), .out13(decoder_1_out13), .out14(decoder_1_out14), .out15(decoder_1_out15),
    .out16(decoder_1_out16), .out17(decoder_1_out17), .out18(decoder_1_out18), .out19(decoder_1_out19),
    .out20(decoder_1_out20), .out21(decoder_1_out21), .out22(decoder_1_out22), .out23(decoder_1_out23),
    .out24(decoder_1_out24), .out25(decoder_1_out25), .out26(decoder_1_out26), .out27(decoder_1_out27),
    .sel(counter_1_pc[4:0]));  // open: out28, out29, out30, out31, en
  Decoder #(.select(5)) decoder_2 (
    .out0(decoder_2_out0), .out1(decoder_2_out1), .out2(decoder_2_out2), .out3(decoder_2_out3),
    .out4(decoder_2_out4), .out5(decoder_2_out5), .out6(decoder_2_out6), .out7(decoder_2_out7),
    .out8(decoder_2_out8), .out9(decoder_2_out9), .out10(decoder_2_out10), .out11(decoder_2_out11),
    .out12(decoder_2_out12), .out13(decoder_2_out13), .out14(decoder_2_out14), .out15(decoder_2_out15),
    .out16(decoder_2_out16), .out17(decoder_2_out17), .out18(decoder_2_out18), .out19(decoder_2_out19),
    .out20(decoder_2_out20), .out21(decoder_2_out21), .out22(decoder_2_out22), .out23(decoder_2_out23),
    .out24(decoder_2_out24), .out25(decoder_2_out25), .out26(decoder_2_out26), .out27(decoder_2_out27),
    .sel(counter_1_pc[4:0]));  // open: out28, out29, out30, out31, en
  or or_1 (L1G, decoder_1_out0, decoder_1_out1, decoder_1_out2, decoder_1_out3, decoder_1_out4, decoder_1_out5, decoder_1_out6, decoder_1_out7);
  or or_2 (L1Y, decoder_1_out8, decoder_1_out9, decoder_1_out10, decoder_1_out11);
  or or_3 (L1R, decoder_1_out12, decoder_1_out13, decoder_1_out14, decoder_1_out15, decoder_1_out16, decoder_1_out17, decoder_1_out18, decoder_1_out19, decoder_1_out20, decoder_1_out21, decoder_1_out22, decoder_1_out23, decoder_1_out24, decoder_1_out25, decoder_1_out26, decoder_1_out27);
  or or_4 (or_4_out, decoder_2_out0, decoder_2_out1, decoder_2_out2, decoder_2_out3, decoder_2_out4, decoder_2_out5, decoder_2_out6, decoder_2_out7, decoder_2_out8, decoder_2_out9, decoder_2_out10, decoder_2_out11, decoder_2_out12, decoder_2_out13);
  or or_5 (L2G, decoder_2_out14, decoder_2_out15, decoder_2_out16, decoder_2_out17, decoder_2_out18, decoder_2_out19, decoder_2_out20, decoder_2_out21);
  or or_6 (L2Y, decoder_2_out22, decoder_2_out23, decoder_2_out24, decoder_2_out25);
  or or_7 (or_7_out, decoder_2_out26, decoder_2_out27);
  or or_8 (L2R, or_4_out, or_7_out);

  // Notes on the sheet:
  //   Light 1
  //   Light 2
endmodule

module stack (
  input  [11:0] Data,
  input  reset,
  input  Push,
  input  Pop,
  input  C,
  output [11:0] Top_of_stack,
  output Error
);

  wire and_2_out, and_3_out, and_4_out, and_5_out, comparator_1_eq, multiplexer_2_out, not_1_out, not_2_out,
       write, xor_1_out;
  wire [11:0] adder_1_out, multiplexer_1_out, multiplexer_3_out, n12_bit_register_1_out_5, subtractor_1_out;

  Adder #(.width(12)) adder_1 (.a(n12_bit_register_1_out_5), .b(12'h1), .out(adder_1_out));  // open: cin, cout
  Subtractor #(.width(12)) subtractor_1 (
    .a(n12_bit_register_1_out_5), .b(12'h1), .out(subtractor_1_out));  // open: bin, bout
  xor xor_1 (xor_1_out, Push, Pop);
  and and_1 (write, xor_1_out, ~Error);  // AND_Gate
  Multiplexer #(.width(12)) multiplexer_1 (
    .in0(adder_1_out), .in1(subtractor_1_out), .out(multiplexer_1_out), .sel(Pop));  // open: en
  Multiplexer multiplexer_2 (.in0(C), .in1(not_1_out), .out(multiplexer_2_out), .sel(and_2_out));  // open: en
  not not_1 (not_1_out, C);
  and and_2 (and_2_out, Push, ~Pop);  // AND_Gate
  _12_bit_register u_12_bit_register_1 (
    .D(multiplexer_1_out), .reset(reset), .write(write), .out_5(n12_bit_register_1_out_5),
    .C(multiplexer_2_out));
  and and_3 (and_3_out, ~Push, Pop);  // AND_Gate
  Multiplexer #(.width(12)) multiplexer_3 (
    .in0(Data), .in1({12{1'b0}}), .out(multiplexer_3_out), .sel(and_3_out));  // open: en
  not not_2 (not_2_out, C);
  RAM #(.addrWidth(12), .dataWidth(12), .bus("separate")) ram_1 (
    .addr(n12_bit_register_1_out_5), .din(multiplexer_3_out), .data(Top_of_stack), .str(write),
    .clk(not_2_out), .ld(1'b1), .clr(reset));  // open: sel
  Comparator #(.width(12), .mode("unsigned")) comparator_1 (
    .a({12{1'b0}}), .b(n12_bit_register_1_out_5), .eq(comparator_1_eq));  // open: gt, lt
  and and_4 (and_4_out, comparator_1_eq, Pop);
  and and_5 (and_5_out, Push, Pop);
  or or_1 (Error, and_4_out, and_5_out);
endmodule
