// Logisim project ALU_Group15.circ as structural Verilog: 15 circuits, main circuit 12-bit ALU
module main (
  output halt,
  output [12:0] counter,
  output [3:0] op,
  output [11:0] a,
  output [11:0] b,
  output [11:0] oracle,
  output [11:0] result,
  output err_oracle,
  output error,
  output ok,
  output start_delimiter
);

  wire and_1_out, and_2_out, clock_1_out, comparator_1_eq, comparator_2_eq;

  Clock clock_1 (.out(clock_1_out));
  Counter #(.width(13), .max('h1fff), .trigger("falling")) counter_1 (
    .Q(counter), .carry(halt), .clk(clock_1_out));  // open: load, D, count, clr
  RAM #(.addrWidth(16), .dataWidth(4), .bus("separate")) ram_1 (
    .addr({counter, 3'b000}), .data(op), .ld(1'b1));  // open: din, str, sel, clk, clr
  RAM #(.addrWidth(16), .dataWidth(12), .bus("separate")) ram_2 (
    .addr({counter, 3'b001}), .data(a), .ld(1'b1));  // open: din, str, sel, clk, clr
  RAM #(.addrWidth(16), .dataWidth(12), .bus("separate")) ram_3 (
    .addr({counter, 3'b010}), .data(b), .ld(1'b1));  // open: din, str, sel, clk, clr
  RAM #(.addrWidth(16), .dataWidth(12), .bus("separate")) ram_4 (
    .addr({counter, 3'b011}), .data(oracle), .ld(1'b1));  // open: din, str, sel, clk, clr
  RAM #(.addrWidth(16), .dataWidth(1), .bus("separate")) ram_5 (
    .addr({counter, 3'b100}), .data(err_oracle), .ld(1'b1));  // open: din, str, sel, clk, clr
  RAM #(.addrWidth(16), .dataWidth(1), .bus("separate")) ram_6 (
    .addr({counter, 3'b101}), .data(start_delimiter), .ld(1'b1));  // open: din, str, sel, clk, clr
  _12_bit_ALU u_12_bit_alu_1 (.ALU_code(op), .a(a), .b(b), .result(result), .Overflow(error));
  Comparator #(.width(1), .mode("unsigned")) comparator_1 (
    .a(error), .b(err_oracle), .eq(comparator_1_eq));  // open: gt, lt
  Comparator #(.width(12)) comparator_2 (.a(result), .b(oracle), .eq(comparator_2_eq));  // open: gt, lt
  and and_1 (and_1_out, comparator_1_eq, error);
  and and_2 (and_2_out, comparator_2_eq, comparator_1_eq, ~error);  // AND_Gate
  or or_1 (ok, and_1_out, and_2_out);

  // Notes on the sheet:
  //   You must complete the circuit '12-bit ALU' instead.
  //   DO NOT EDIT THIS CIRCUIT!
endmodule

module _12_bit_ALU (
  input  [3:0] ALU_code,
  input  [11:0] a,
  input  [11:0] b,
  output [11:0] result,
  output Overflow
);

  wire addoverflow, invoverflow, slaoverflow, suboverflow;
  wire [11:0] and_out, equals_1_equal, generate_0_1_out_1, greater_than_1_greater_than,
       less_than_1_less_than, no_operation_1_out_2, not_equals_1_not_equals, not_out, numeric_addition_1_sum,
       numeric_inverse_1_two_s_complement_of_a, numeric_subtraction_1_sub, or_out,
       shift_left_arithmetic_1_out_3, shift_left_logical_1_out_2, shift_right_arithmetic_1_out_2,
       shift_right_logical_1_out_2;

  Numeric_Addition numeric_addition_1 (.a(a), .b(b), .Sum(numeric_addition_1_sum), .Overflow(addoverflow));
  Numeric_Subtraction numeric_subtraction_1 (.a(a), .b(b), .Sub(numeric_subtraction_1_sub), .Overflow(suboverflow));
  assign and_out = a & b;  // AND_Gate and, 12 bits wide
  assign or_out = a | b;  // OR_Gate or, 12 bits wide
  less_than less_than_1 (.a(a), .b(b), .Less_than(less_than_1_less_than));
  greater_than greater_than_1 (.a(a), .b(b), .Greater_than(greater_than_1_greater_than));
  equals equals_1 (.a(a), .b(b), .equal(equals_1_equal));
  not_equals not_equals_1 (.a(a), .b(b), .not_equals(not_equals_1_not_equals));
  assign not_out = ~a;  // NOT_Gate not, 12 bits wide
  numeric_inverse numeric_inverse_1 (
    .a(a), .two_s_complement_of_a(numeric_inverse_1_two_s_complement_of_a), .Overflow(invoverflow));
  shift_left_logical shift_left_logical_1 (.a(a), .out_2(shift_left_logical_1_out_2));
  shift_right_logical shift_right_logical_1 (.a(a), .out_2(shift_right_logical_1_out_2));
  shift_left_arithmetic shift_left_arithmetic_1 (.a(a), .out_3(shift_left_arithmetic_1_out_3), .Overflow(slaoverflow));
  shift_right_arithmetic shift_right_arithmetic_1 (.a(a), .out_2(shift_right_arithmetic_1_out_2));
  generate_0 generate_0_1 (.out_1(generate_0_1_out_1));
  no_operation no_operation_1 (.in_1(a), .out_2(no_operation_1_out_2));
  Multiplexer #(.select(4), .width(12)) multiplexer_1 (
    .in0(numeric_addition_1_sum), .in1(numeric_subtraction_1_sub), .in2(and_out), .in3(or_out),
    .in4(less_than_1_less_than), .in5(greater_than_1_greater_than), .in6(equals_1_equal),
    .in7(not_equals_1_not_equals), .in8(not_out), .in9(numeric_inverse_1_two_s_complement_of_a),
    .in10(shift_left_logical_1_out_2), .in11(shift_right_logical_1_out_2),
    .in12(shift_left_arithmetic_1_out_3), .in13(shift_right_arithmetic_1_out_2), .in14(generate_0_1_out_1),
    .in15(no_operation_1_out_2), .out(result), .sel(ALU_code));  // open: en
  Multiplexer #(.select(4)) multiplexer_2 (
    .in0(addoverflow), .in1(suboverflow), .in2(1'b0), .in3(1'b0), .in4(1'b0), .in5(1'b0), .in6(1'b0),
    .in7(1'b0), .in8(1'b0), .in9(invoverflow), .in10(1'b0), .in11(1'b0), .in12(slaoverflow), .in13(1'b0),
    .in14(1'b0), .in15(1'b0), .out(Overflow), .sel(ALU_code));  // open: en

  // Other names for the same wires on the sheet: alucode[3:0] = ALU_code

  // Notes on the sheet:
  //   This circuit is used as a block in the main circuit, and its layout must remain unchanged. The circuit called "main" should be the main circuit of this file.
  //   Do not change the circuit appearance.
  //   DO NOT CHANGE THE INPUTS AND OUTPUTS OF THIS CIRCUIT!
  //   Do not add/remove inputs or outputs. Do not even change their location or orientation.
endmodule

// add
module Numeric_Addition (
  input  [11:0] a,
  input  [11:0] b,
  output [11:0] Sum,
  output Overflow
);

  // Probe on a
  // Probe on b
  _12_Bit_CLA Add (.A(a), .Sum(Sum), .B(b), .C0(1'b0), .Overflow(Overflow));  // open: C4
  // Probe on Sum
endmodule

// sub
module Numeric_Subtraction (
  input  [11:0] a,
  input  [11:0] b,
  output [11:0] Sub,
  output Overflow
);

  wire and_1_out, and_2_out;
  wire [11:0] not_1_out;

  // Probe on a
  // Probe on b
  assign not_1_out = ~b;  // NOT_Gate not_1, 12 bits wide
  _12_Bit_CLA u_12_bit_cla_1 (.A(a), .Sum(Sub), .B(not_1_out), .C0(1'b1));  // open: C4, Overflow
  // Probe on Sub
  and and_1 (and_1_out, ~not_1_out[11], ~a[11], Sub[11]);  // AND_Gate
  and and_2 (and_2_out, ~Sub[11], a[11], not_1_out[11]);  // AND_Gate
  or or_1 (Overflow, and_1_out, and_2_out);
endmodule

// lt
module less_than (
  input  [11:0] a,
  input  [11:0] b,
  output [11:0] Less_than
);

  wire if_the_first_number_is_negative_and_the_second_one_is_positive_out,
       if_the_result_is_negative_and_there_is_no_overflow_out, numeric_subtraction_1_overflow;
  wire [11:0] numeric_subtraction_1_sub;

  // Probe on a
  // Probe on b
  Numeric_Subtraction numeric_subtraction_1 (
    .a(a), .b(b), .Sub(numeric_subtraction_1_sub), .Overflow(numeric_subtraction_1_overflow));
  and if_the_first_number_is_negative_and_the_second_one_is_positive (if_the_first_number_is_negative_and_the_second_one_is_positive_out, a[11], ~b[11]);  // AND_Gate
  and if_the_result_is_negative_and_there_is_no_overflow (if_the_result_is_negative_and_there_is_no_overflow_out, numeric_subtraction_1_sub[11], ~numeric_subtraction_1_overflow);  // AND_Gate
  or or_1 (Less_than[0], if_the_first_number_is_negative_and_the_second_one_is_positive_out, if_the_result_is_negative_and_there_is_no_overflow_out);

  assign Less_than[11:1] = {11{1'b0}};
endmodule

// gt
module greater_than (
  input  [11:0] a,
  input  [11:0] b,
  output [11:0] Greater_than
);

  wire if_the_first_number_is_negative_and_the_second_one_is_positive_out,
       if_the_result_is_positive_and_there_is_no_overflow_out, numeric_subtraction_1_overflow;
  wire [11:0] not_equals_1_not_equals, numeric_subtraction_1_sub;

  // Probe on a
  // Probe on b
  Numeric_Subtraction numeric_subtraction_1 (
    .a(a), .b(b), .Sub(numeric_subtraction_1_sub), .Overflow(numeric_subtraction_1_overflow));
  and if_the_first_number_is_negative_and_the_second_one_is_positive (if_the_first_number_is_negative_and_the_second_one_is_positive_out, ~a[11], b[11]);  // AND_Gate
  not_equals not_equals_1 (.a(numeric_subtraction_1_sub), .b({12{1'b0}}), .not_equals(not_equals_1_not_equals));
  and if_the_result_is_positive_and_there_is_no_overflow (if_the_result_is_positive_and_there_is_no_overflow_out, not_equals_1_not_equals[0], ~numeric_subtraction_1_sub[11], ~numeric_subtraction_1_overflow);  // AND_Gate
  or or_1 (Greater_than[0], if_the_first_number_is_negative_and_the_second_one_is_positive_out, if_the_result_is_positive_and_there_is_no_overflow_out);

  assign Greater_than[11:1] = {11{1'b0}};

  // Notes on the sheet:
  //   not equals 0
endmodule

// eq
module equals (
  input  [11:0] a,
  input  [11:0] b,
  output [11:0] equal
);

  wire [11:0] not_1_out, numeric_subtraction_1_sub;

  // Probe on a
  // Probe on b
  Numeric_Subtraction numeric_subtraction_1 (.a(a), .b(b), .Sub(numeric_subtraction_1_sub));  // open: Overflow
  assign not_1_out = ~numeric_subtraction_1_sub;  // NOT_Gate not_1, 12 bits wide
  and and_1 (equal[0], not_1_out[0], not_1_out[1], not_1_out[2], not_1_out[3], not_1_out[4], not_1_out[5], not_1_out[6], not_1_out[7], not_1_out[8], not_1_out[9], not_1_out[10], not_1_out[11]);

  assign equal[11:1] = {11{1'b0}};
endmodule

// neq
module not_equals (
  input  [11:0] a,
  input  [11:0] b,
  output [11:0] not_equals
);

  wire and_1_out;
  wire [11:0] not_1_out, numeric_subtraction_1_sub;

  // Probe on a
  // Probe on b
  Numeric_Subtraction numeric_subtraction_1 (.a(a), .b(b), .Sub(numeric_subtraction_1_sub));  // open: Overflow
  assign not_1_out = ~numeric_subtraction_1_sub;  // NOT_Gate not_1, 12 bits wide
  not not_2 (not_equals[0], and_1_out);
  and and_1 (and_1_out, not_1_out[0], not_1_out[1], not_1_out[2], not_1_out[3], not_1_out[4], not_1_out[5], not_1_out[6], not_1_out[7], not_1_out[8], not_1_out[9], not_1_out[10], not_1_out[11]);

  assign not_equals[11:1] = {11{1'b0}};
endmodule

// inv
module numeric_inverse (
  input  [11:0] a,
  output [11:0] two_s_complement_of_a,
  output Overflow
);

  wire [11:0] not_1_out;

  // Probe on a
  assign not_1_out = ~a;  // NOT_Gate not_1, 12 bits wide
  // Probe on two_s_complement_of_a
  Numeric_Addition numeric_addition_1 (.a(12'h1), .b(not_1_out), .Sum(two_s_complement_of_a), .Overflow(Overflow));
endmodule

// sll
module shift_left_logical (
  input  [11:0] a,
  output [11:0] out_2
);

  // Probe on a
  // Probe on {a[10:0], 1'b0}

  assign out_2 = {a[10:0], 1'b0};
endmodule

// srl
module shift_right_logical (
  input  [11:0] a,
  output [11:0] out_2
);

  // Probe on a
  // Probe on {1'b0, a[11:1]}

  assign out_2 = {1'b0, a[11:1]};
endmodule

// sra
module shift_right_arithmetic (
  input  [11:0] a,
  output [11:0] out_2
);

  // Probe on a
  // Probe on {{2{a[11]}}, a[10:1]}

  assign out_2 = {{2{a[11]}}, a[10:1]};
endmodule

// sla
module shift_left_arithmetic (
  input  [11:0] a,
  output Overflow,
  output [11:0] out_3
);

  xor xor_1 (Overflow, a[11], a[10]);
  // Probe on a
  // Probe on {a[10:0], 1'b0}

  assign out_3 = {a[10:0], 1'b0};
endmodule

// zero
module generate_0 (
  output [11:0] out_1
);


  assign out_1 = {12{1'b0}};
endmodule

// noop
module no_operation (
  input  [11:0] in_1,
  output [11:0] out_2
);


  assign out_2 = in_1;
endmodule
